# Fritzing sketch RpiZero2W (saved by Fritzing 1.0.5)

parts:
  MCU1 = Raspberry Pi Zero
  OLed = Grove OLED 128x96
  J1 = Basic Servo
  V1 = DC Power [voltage=5V]

nets:
  N1: MCU1.pin_1, MCU1.pin_17, OLed.VCC
  N2: MCU1.pin_3, OLed.SDA
  N3: MCU1.pin_5, OLed.SCL
  GND: MCU1.pin_6, MCU1.pin_14, MCU1.pin_30, MCU1.pin_39, OLed.GND, J1.gnd, V1.V-
  N4: MCU1.pin_12, J1.pulse
  N5: J1.vcc, V1.V+
